// Logisim project VL_Counter.circ as structural Verilog: 1 circuit, main circuit main
module main (
);

  wire and_1_out, and_2_out, button_1_out, clock_1_out, main_1_p5, main_2_p5, main_3_p5, multiplexer_1_out,
       multiplexer_2_out, multiplexer_3_out, t_ff_1_q;
  wire [3:0] main_1_p4;

  Button button_1 (.out(button_1_out));
  Clock clock_1 (.out(clock_1_out));
  T_Flip_Flop t_ff_1 (.T(1'b1), .clk(button_1_out), .Q(t_ff_1_q));  // open: Qn, reset, preset
  LED led_1 (.in(main_1_p4[0]));
  // JK_Retard_main main_1: pin names not known; wires that end beside it: 1'b1, clock_1_out, 1'b1, main_1_p4[0], main_1_p5
  // Probe on main_1_p4
  Multiplexer #(.enable("false")) multiplexer_1 (
    .in0(main_1_p4[0]), .in1(main_1_p5), .out(multiplexer_1_out), .sel(t_ff_1_q));
  // JK_Retard_main main_2: pin names not known; wires that end beside it: multiplexer_1_out, clock_1_out, multiplexer_1_out, main_1_p4[1], main_2_p5
  and and_1 (and_1_out, multiplexer_1_out, multiplexer_2_out);
  Multiplexer #(.enable("false")) multiplexer_2 (
    .in0(main_1_p4[1]), .in1(main_2_p5), .out(multiplexer_2_out), .sel(t_ff_1_q));
  // JK_Retard_main main_3: pin names not known; wires that end beside it: and_1_out, clock_1_out, and_1_out, main_1_p4[2], main_3_p5
  and and_2 (and_2_out, and_1_out, multiplexer_3_out);
  Multiplexer #(.enable("false")) multiplexer_3 (
    .in0(main_1_p4[2]), .in1(main_3_p5), .out(multiplexer_3_out), .sel(t_ff_1_q));
  // JK_Retard_main main_4: pin names not known; wires that end beside it: and_2_out, clock_1_out, and_2_out, main_1_p4[3]
endmodule
