// Logisim project Zaehler2.circ as structural Verilog: 1 circuit, main circuit main
module main (
  input  A,
  output [7:0] Zahl
);

  wire [7:0] register_1_q;
  wire [7:2] and_1_out;

  // Probe on {and_1_out, register_1_q[0], 1'b1}
  Register register_1 (.D(Zahl), .en(1'b1), .Q(register_1_q), .clk(A), .clr(1'b0));
  assign Zahl = register_1_q ^ {and_1_out, register_1_q[0], 1'b1};  // XOR_Gate xor_1, 8 bits wide
  and and_1 (and_1_out[2], register_1_q[0], register_1_q[1]);
  and and_2 (and_1_out[3], and_1_out[2], register_1_q[2]);
  and and_3 (and_1_out[4], and_1_out[3], register_1_q[3]);
  and and_4 (and_1_out[5], and_1_out[4], register_1_q[4]);
  and and_5 (and_1_out[6], and_1_out[5], register_1_q[5]);
  and and_6 (and_1_out[7], and_1_out[6], register_1_q[6]);
endmodule
