// Logisim project Volladdierer.circ as structural Verilog: 1 circuit, main circuit main
module main (
);

  wire adder_1_cout, adder_2_cout, adder_3_cout, adder_4_cout, adder_5_cout, button_1_out, clock_1_out,
       clock_2_out, clock_3_out, d_ff_1_q, j_k_ff_1_q, j_k_ff_1_qn, s_r_ff_1_q, s_r_ff_1_qn, xor_1_out;
  wire [3:0] adder_1_out, adder_2_out, adder_3_out, adder_4_out, random_1_out, random_1_out_2,
       random_1_out_3, random_1_out_4, random_1_out_5, random_1_out_6, random_1_out_7, random_1_out_8;
  wire [15:0] adder_5_out;

  Clock #(.highDuration(50), .lowDuration(50)) clock_1 (.out(clock_1_out));
  Button button_1 (.out(button_1_out));
  Hex_Digit_Display hex_digit_display_1 (.value(random_1_out_7), .dp(1'b0));
  Hex_Digit_Display hex_digit_display_2 (.value(random_1_out_8), .dp(1'b0));
  Random #(.width(32)) random_1 (
    .clk(xor_1_out), .next(1'b1),
    .out({random_1_out_8, random_1_out_7, random_1_out_6, random_1_out_5, random_1_out_4, random_1_out_3, random_1_out_2, random_1_out}),
    .clr(1'b0));
  xor xor_1 (xor_1_out, clock_1_out, button_1_out);
  Clock #(.highDuration(13), .lowDuration(13)) clock_2 (.out(clock_2_out));
  Hex_Digit_Display hex_digit_display_3 (.value(random_1_out_5), .dp(1'b0));
  Hex_Digit_Display hex_digit_display_4 (.value(random_1_out_6), .dp(1'b0));
  LED led_1 (.in(clock_2_out));
  Hex_Digit_Display hex_digit_display_5 (.value(random_1_out_4), .dp(1'b0));
  Adder #(.width(4)) adder_1 (.a(random_1_out), .b(random_1_out_5), .out(adder_1_out), .cin(1'b0), .cout(adder_1_cout));
  Adder #(.width(4)) adder_2 (
    .a(random_1_out_2), .b(random_1_out_6), .out(adder_2_out), .cin(adder_1_cout), .cout(adder_2_cout));
  Adder #(.width(4)) adder_3 (
    .a(random_1_out_3), .b(random_1_out_7), .out(adder_3_out), .cin(adder_2_cout), .cout(adder_3_cout));
  Adder #(.width(4)) adder_4 (
    .a(random_1_out_4), .b(random_1_out_8), .out(adder_4_out), .cin(adder_3_cout), .cout(adder_4_cout));
  Clock #(.highDuration(10), .lowDuration(10)) clock_3 (.out(clock_3_out));
  Hex_Digit_Display hex_digit_display_6 (.value(random_1_out_3), .dp(1'b0));
  Hex_Digit_Display hex_digit_display_7 (.value(random_1_out_2), .dp(1'b0));
  Adder #(.width(16)) adder_5 (
    .a({random_1_out_4, random_1_out_3, random_1_out_2, random_1_out}),
    .b({random_1_out_8, random_1_out_7, random_1_out_6, random_1_out_5}), .out(adder_5_out), .cin(1'b0),
    .cout(adder_5_cout));
  RAM #(.dataWidth(32)) ram_1 ();  // open: addr, data, sel, clk, ld, clr
  Hex_Digit_Display hex_digit_display_8 (.value(random_1_out), .dp(1'b0));
  D_Flip_Flop d_ff_1 (.clk(clock_2_out), .D(clock_3_out), .Q(d_ff_1_q));  // open: Qn, preset, en, reset
  Hex_Digit_Display hex_digit_display_9 (.value(adder_5_out[15:12]), .dp(1'b0));
  Hex_Digit_Display hex_digit_display_10 (.value(adder_4_out), .dp(adder_1_cout));
  T_Flip_Flop t_ff_1 (.clk(clock_3_out), .T(d_ff_1_q));  // open: Q, Qn, preset, reset, en
  Hex_Digit_Display hex_digit_display_11 (.value(adder_5_out[7:4]), .dp(1'b0));
  Hex_Digit_Display hex_digit_display_12 (.value(adder_5_out[11:8]), .dp(1'b0));
  Hex_Digit_Display hex_digit_display_13 (.value(adder_2_out), .dp(adder_3_cout));
  Hex_Digit_Display hex_digit_display_14 (.value(adder_3_out), .dp(adder_2_cout));
  Hex_Digit_Display hex_digit_display_15 (.value(adder_5_out[3:0]), .dp(adder_5_cout));
  Hex_Digit_Display hex_digit_display_16 (.value(adder_1_out), .dp(adder_4_cout));
  LED led_2 (.in(j_k_ff_1_q));
  J_K_Flip_Flop j_k_ff_1 (
    .J(1'b1), .clk(clock_3_out), .K(1'b1), .Q(j_k_ff_1_q), .Qn(j_k_ff_1_qn), .preset(1'b0), .en(1'b1),
    .reset(1'b0));
  LED led_3 (.in(j_k_ff_1_qn));
  LED led_4 (.in(s_r_ff_1_q));
  S_R_Flip_Flop s_r_ff_1 (
    .S(1'b0), .clk(clock_3_out), .R(1'b1), .Q(s_r_ff_1_q), .Qn(s_r_ff_1_qn), .preset(1'b0), .reset(1'b0),
    .en(1'b1));
  LED led_5 (.in(s_r_ff_1_qn));
endmodule
